# Fritzing sketch SingleDice (saved by Fritzing 0.9.2b)
circuit board: 11.225cm x 4.80834cm
breadboards: 1

parts:
  JP1 = Header 2 [package=screwterminal-3.5mm-2_lock]
  Atmega328P = atmega328 [package=dip]
  TRIGGER = SWITCH-MOMENTARY-2 [package=tactile-pth-12mm]
  R3 = Resistor [tolerance=±5% resistance=100 package=THT]
  R8 = Resistor [tolerance=±5% resistance=100 package=THT]
  R5_-_R8 = Resistor [tolerance=±5% resistance=100 package=THT]
  PCF8574 = PCF8574 [package="DIP16 [THT]"]
  R2 = Resistor [tolerance=±5% resistance=100 package=THT]
  R1 = Resistor [tolerance=±5% resistance=100 package=THT]
  R1_-_R4 = Resistor [tolerance=±5% resistance=100 package=THT]
  8_SEGMENT = 7-Segment LED Display [package=THT]
  R5 = Resistor [tolerance=±5% resistance=100 package=THT]
  R6 = Resistor [tolerance=±5% resistance=100 package=THT]
  LED1 = LED - 5mm [color="Red (633nm)" package="5 mm [THT]"]
  LED2 = LED - 5mm [color="Red (633nm)" package="5 mm [THT]"]
  LED3 = LED - 5mm [color="Red (633nm)" package="5 mm [THT]"]
  LED4 = LED - 5mm [color="Red (633nm)" package="5 mm [THT]"]
  LED1_-_LED5 = LED - 5mm [color="Red (633nm)" package="5 mm [THT]"]
  R13 = Resistor [tolerance=±5% resistance=220 package=THT]
  R12 = Resistor [tolerance=±5% resistance=220 package=THT]
  R11 = Resistor [tolerance=±5% resistance=220 package=THT]
  R10 = Resistor [tolerance=±5% resistance=220 package=THT]
  R9_-_R13 = Resistor [tolerance=±5% resistance=220 package=THT]

nets:
  N1: JP1.1, Atmega328P.VCC, Atmega328P.AVCC, 8_SEGMENT.commAnode#7
  GND: JP1.2, Atmega328P.GND, TRIGGER.2, PCF8574.A0, PCF8574.A1, PCF8574.A3, PCF8574.GND, LED1.cathode, LED2.cathode, LED3.cathode, LED4.cathode, LED1_-_LED5.cathode
  N2: Atmega328P.D8, TRIGGER.1
  N3: Atmega328P.D9_(PWM), R13.Pin_0
  N4: Atmega328P.D10_(PWM), R12.Pin_0
  N5: Atmega328P.D11_(PWM), R11.Pin_0
  N6: Atmega328P.D12, R10.Pin_0
  N7: Atmega328P.D13, R9_-_R13.Pin_0
  N8: Atmega328P.A4, PCF8574.SDA
  N9: Atmega328P.A5, PCF8574.SCL
  N10: R3.Pin_0, PCF8574.P1
  N11: R3.Pin_1, 8_SEGMENT.cathodeC
  N12: R8.Pin_0, PCF8574.P7
  N13: R8.Pin_1, 8_SEGMENT.cathodeF
  N14: R5_-_R8.Pin_0, PCF8574.P6
  N15: R5_-_R8.Pin_1, 8_SEGMENT.cathodeG
  N16: PCF8574.P0, R1_-_R4.Pin_0
  N17: PCF8574.P2, R2.Pin_0
  N18: PCF8574.P3, R1.Pin_0
  N19: PCF8574.P4, R5.Pin_0
  N20: PCF8574.P5, R6.Pin_0
  N21: PCF8574.VCC, 8_SEGMENT.commAnode#2
  N22: R2.Pin_1, 8_SEGMENT.cathodeD
  N23: R1.Pin_1, 8_SEGMENT.cathodeE
  N24: R1_-_R4.Pin_1, 8_SEGMENT.cathodeDP
  N25: 8_SEGMENT.cathodeB, R5.Pin_1
  N26: 8_SEGMENT.cathodeA, R6.Pin_1
  N27: LED1.anode, R9_-_R13.Pin_1
  N28: LED2.anode, R10.Pin_1
  N29: LED3.anode, R11.Pin_1
  N30: LED4.anode, R12.Pin_1
  N31: LED1_-_LED5.anode, R13.Pin_1

notes:
  pomek.pl
  Single Dice
  3.3V
